# Fritzing sketch Breadboard (saved by Fritzing 0.8.3b)
breadboards: 1

parts:
  DHT1 = DHT11 Humitidy and Temperature Sensor
  Part1 = Arduino Uno (Rev3)
  LCD1 = LCD screen

nets:
  VDD: DHT1.VDD, Part1.5V, LCD1.VDD, LCD1.LED+
  N1: DHT1.DATA, Part1.D2
  GND: DHT1.GND, Part1.GND, LCD1.VSS, LCD1.LED-
  N2: Part1.D10_PWM/SS, LCD1.DB4
  N3: Part1.D11_PWM/MOSI, LCD1.DB5
  N4: Part1.D12/MISO, LCD1.DB6
  N5: Part1.D13/SCK, LCD1.DB7
  N6: Part1.D3_PWM, LCD1.RS
  N7: Part1.D4, LCD1.R/W
  N8: Part1.D5_PWM, LCD1.E
  N9: Part1.D6_PWM, LCD1.V0

custom parts:
  DHT11 Humitidy and Temperature Sensor: DHT11 Humidity and Temperature Sensor
